# Fritzing sketch vfobfo_schematic (saved by Fritzing 0.9.3b)
breadboards: 1

parts:
  Arduino_ATmega32U4 = Arduino Micro (Rev3)
  OLED = Grove OLED 128x96
  Band = SWITCH-MOMENTARY-2 [package=tactile-pth-12mm]
  Step = SWITCH-MOMENTARY-2 [package=tactile-pth-12mm]
  R1 = Resistor [tolerance=±5% resistance=10 package=THT]
  R2 = Resistor [tolerance=±5% resistance=10 package=THT]
  Si5351 = Grove OLED 128x96  # not connected

nets:
  N1: Arduino_ATmega32U4.D1/TX, Step.1, R1.Pin_1
  N2: Arduino_ATmega32U4.D0/RX, Band.1, R2.Pin_1
  GND: Arduino_ATmega32U4.GND, OLED.GND, Band.2, Step.2, R1.Pin_0, R2.Pin_0
  N3: Arduino_ATmega32U4.D2/SDA, OLED.SDA
  N4: Arduino_ATmega32U4.D3/SCL, OLED.SCL
  5V: OLED.VCC
